// Logisim project ALU.circ as structural Verilog
// ALU 1Bit
module ALU_1_bit (
  input  A,
  input  B,
  input  C_i,
  input  [2:0] in_4,
  output C_o,
  output out_6
);

  wire and_1_out, full_adder_1_bit_1_p4, nand_1_out, nor_1_out, not_1_out, or_1_out, xnor_1_out, xor_1_out;

  // FULL_ADDER_1_Bit full_adder_1_bit_1: pin names not known; wires that end beside it: A, B, C_i, full_adder_1_bit_1_p4, C_o
  not not_1 (not_1_out, B);
  xor xor_1 (xor_1_out, A, B);
  nor nor_1 (nor_1_out, A, B);
  and and_1 (and_1_out, A, B);
  or or_1 (or_1_out, A, B);
  nand nand_1 (nand_1_out, A, B);
  xnor xnor_1 (xnor_1_out, A, B);
  MUX_8__1_1Bit mux_8_1_1bit_1 (
    .in_1(xor_1_out), .in_2(nor_1_out), .in_3(full_adder_1_bit_1_p4), .in_4(and_1_out), .in_5(or_1_out),
    .in_6(not_1_out), .in_7(nand_1_out), .in_8(xnor_1_out), .out_10(out_6), .in_9(in_4));
endmodule

// ALU
module ALU_PROC (
  input  [3:0] in_1,
  input  [3:0] in_2,
  input  Ci,
  input  [2:0] S,
  output Co,
  output [3:0] out_6
);

  wire alu_1_bit_1_c_o, alu_1_bit_2_c_o, alu_1_bit_3_c_o;

  ALU_1_bit alu_1_bit_1 (.C_i(Ci), .A(in_1[0]), .B(in_2[0]), .C_o(alu_1_bit_1_c_o), .out_6(out_6[0]), .in_4(S));
  ALU_1_bit alu_1_bit_2 (
    .C_i(alu_1_bit_1_c_o), .A(in_1[1]), .B(in_2[1]), .C_o(alu_1_bit_2_c_o), .out_6(out_6[1]), .in_4(S));
  ALU_1_bit alu_1_bit_3 (
    .C_i(alu_1_bit_2_c_o), .A(in_1[2]), .B(in_2[2]), .C_o(alu_1_bit_3_c_o), .out_6(out_6[2]), .in_4(S));
  ALU_1_bit alu_1_bit_4 (.C_i(alu_1_bit_3_c_o), .A(in_1[3]), .B(in_2[3]), .C_o(Co), .out_6(out_6[3]), .in_4(S));
endmodule

// MUX 4BIT
module MUX_8__1_4BIT (
  input  [3:0] in_1,
  input  [3:0] in_2,
  input  [3:0] in_3,
  input  [3:0] in_4,
  input  [3:0] in_5,
  input  [3:0] in_6,
  input  [3:0] in_7,
  input  [3:0] in_8,
  input  [2:0] in_9,
  output [3:0] out_10
);

  MUX_8__1_1Bit mux_8_1_1bit_1 (
    .in_1(in_1[0]), .in_2(in_2[0]), .in_3(in_3[0]), .in_4(in_4[0]), .in_5(in_5[0]), .in_6(in_6[0]),
    .in_7(in_7[0]), .in_8(in_8[0]), .out_10(out_10[0]), .in_9(in_9));
  MUX_8__1_1Bit mux_8_1_1bit_2 (
    .in_1(in_1[1]), .in_2(in_2[1]), .in_3(in_3[1]), .in_4(in_4[1]), .in_5(in_5[1]), .in_6(in_6[1]),
    .in_7(in_7[1]), .in_8(in_8[1]), .out_10(out_10[1]), .in_9(in_9));
  MUX_8__1_1Bit mux_8_1_1bit_3 (
    .in_1(in_1[2]), .in_2(in_2[2]), .in_3(in_3[2]), .in_4(in_4[2]), .in_5(in_5[2]), .in_6(in_6[2]),
    .in_7(in_7[2]), .in_8(in_8[2]), .out_10(out_10[2]), .in_9(in_9));
  MUX_8__1_1Bit mux_8_1_1bit_4 (
    .in_1(in_1[3]), .in_2(in_2[3]), .in_3(in_3[3]), .in_4(in_4[3]), .in_5(in_5[3]), .in_6(in_6[3]),
    .in_7(in_7[3]), .in_8(in_8[3]), .out_10(out_10[3]), .in_9(in_9));
endmodule
