// Logisim project CU.circ as structural Verilog
module UC (
  input  [11:0] In_in,
  input  [3:0] PCin,
  input  RESET,
  output Fetch,
  output wAD,
  output Write,
  output Source_Sel,
  output [1:0] RWrite_Sel,
  output [3:0] RX_Sel,
  output [3:0] RY_Sel,
  output [2:0] ALU_Sel,
  output [3:0] mAD,
  output [3:0] PCout,
  output wPC
);

  wire [3:0] XSel_selcode, Ysel_selcode;

  PC_Increase pc_increase_1 (.in(PCin), .RESET(RESET), .out(PCout));
  DecSel XSel (.In(In_in[3:2]), .SelCode(XSel_selcode));
  DecSel Ysel (.In(In_in[5:4]), .SelCode(Ysel_selcode));
  RegW regw_1 (.OPCODE(In_in[11:8]), .Write(Write));
  Clock CLK (.out(wPC));
  WriteAD writead_1 (.OPCODE(In_in[11:8]), .wAD(wAD));
  SourceSel sourcesel_1 (.OPCODE(In_in[11:8]), .Write(Source_Sel));
  ReadSelector readselector_1 (
    .X_in(XSel_selcode), .Y_in(Ysel_selcode), .X_out(RX_Sel), .Y_out(RY_Sel), .OPCODE(In_in[11:8]));
  ALU_Function alu_function_1 (.OPCODE(In_in[11:8]), .ALUCODE(ALU_Sel));

  assign Fetch = 1'b1;
  assign mAD = In_in[5:2];
  assign RWrite_Sel = In_in[7:6];

  // Notes on the sheet:
  //   REG_Dest
  //   OPCODE
endmodule

// F_ALU
module ALU_Function (
  input  [3:0] OPCODE,
  output [2:0] ALUCODE
);


  assign ALUCODE = {1'b0, OPCODE[1:0]};
endmodule

// S_Sel
module SourceSel (
  input  [3:0] OPCODE,
  output Write
);

  wire not_1_out, not_2_out, not_3_out;

  not not_1 (not_1_out, OPCODE[0]);
  not not_2 (not_2_out, OPCODE[1]);
  not not_3 (not_3_out, OPCODE[3]);
  and and_1 (Write, not_1_out, not_2_out, OPCODE[2], not_3_out);
endmodule

// wAD_F
module WriteAD (
  input  [3:0] OPCODE,
  output wAD
);

  wire not_1_out, not_2_out, not_3_out;

  not not_1 (not_1_out, OPCODE[0]);
  not not_2 (not_2_out, OPCODE[1]);
  not not_3 (not_3_out, OPCODE[2]);
  and and_1 (wAD, not_1_out, not_2_out, not_3_out, OPCODE[3]);
endmodule

module Imm_Format (
  input  [3:0] OPCODE,
  output wAD
);

  wire and_1_out, and_2_out, not_1_out, not_2_out, not_3_out, not_4_out, not_5_out, not_6_out;

  not not_1 (not_1_out, OPCODE[0]);
  not not_2 (not_2_out, OPCODE[1]);
  not not_3 (not_3_out, OPCODE[3]);
  not not_4 (not_4_out, OPCODE[0]);
  not not_5 (not_5_out, OPCODE[1]);
  not not_6 (not_6_out, OPCODE[2]);
  and and_1 (and_1_out, not_1_out, not_2_out, OPCODE[2], not_3_out);
  and and_2 (and_2_out, not_4_out, not_5_out, not_6_out, OPCODE[3]);
  or or_1 (wAD, and_1_out, and_2_out);
endmodule

module PC_Increase (
  input  [3:0] in,
  input  RESET,
  output [3:0] out
);

  wire full_adder_1_bit_1_c_o, full_adder_1_bit_2_c_o, half_adder_1_out_4, not_1_out;
  wire [3:0] half_adder_1_s;

  HALF_ADDER half_adder_1 (.A(in[0]), .B(1'b1), .out_4(half_adder_1_out_4), .S(half_adder_1_s[0]));
  FULL_ADDER_1_Bit full_adder_1_bit_1 (
    .A(in[1]), .B(1'b0), .C_i(half_adder_1_out_4), .S(half_adder_1_s[1]), .C_o(full_adder_1_bit_1_c_o));
  FULL_ADDER_1_Bit full_adder_1_bit_2 (
    .A(in[2]), .B(1'b0), .C_i(full_adder_1_bit_1_c_o), .S(half_adder_1_s[2]), .C_o(full_adder_1_bit_2_c_o));
  FULL_ADDER_1_Bit full_adder_1_bit_3 (
    .A(in[3]), .B(1'b0), .C_i(full_adder_1_bit_2_c_o), .S(half_adder_1_s[3]));  // open: C_o
  Multiplexer #(.width(4), .enable("false")) multiplexer_1 (
    .in0(4'b0000), .in1(half_adder_1_s), .out(out), .sel(not_1_out));
  not not_1 (not_1_out, RESET);
endmodule

module RegW (
  input  [3:0] OPCODE,
  output Write
);

  wire and_1_out, not_1_out, not_2_out, not_3_out;

  not not_1 (not_1_out, OPCODE[0]);
  not not_2 (not_2_out, OPCODE[1]);
  not not_3 (not_3_out, OPCODE[2]);
  and and_1 (and_1_out, not_1_out, not_2_out, not_3_out, OPCODE[3]);
  not not_4 (Write, and_1_out);
endmodule

module DecSel (
  input  [1:0] In,
  output [3:0] SelCode
);

  // DEC_1_4 dec_1_4_1: pin names not known; wires that end beside it: In, SelCode[0], SelCode[1], SelCode[2], SelCode[3]
endmodule

// ReadSel
module ReadSelector (
  input  [3:0] X_in,
  input  [3:0] Y_in,
  input  [3:0] OPCODE,
  output [3:0] X_out,
  output [3:0] Y_out
);

  wire not_1_out, not_2_out, not_3_out, not_4_out, not_5_out, xnor_1_out;
  wire [3:0] controlled_buffer_1_out, controlled_buffer_3_out;

  assign controlled_buffer_1_out = not_2_out ? X_in : 4'bz;  // Controlled_Buffer controlled_buffer_1
  assign controlled_buffer_1_out = not_1_out ? 4'b0000 : 4'bz;  // Controlled_Buffer controlled_buffer_2
  not not_1 (not_1_out, not_2_out);
  not not_2 (not_2_out, OPCODE[2]);
  assign controlled_buffer_3_out = xnor_1_out ? Y_in : 4'bz;  // Controlled_Buffer controlled_buffer_3
  assign controlled_buffer_3_out = not_3_out ? 4'b0000 : 4'bz;  // Controlled_Buffer controlled_buffer_4
  not not_3 (not_3_out, xnor_1_out);
  xnor xnor_1 (xnor_1_out, not_5_out, not_4_out);
  not not_4 (not_4_out, OPCODE[3]);
  not not_5 (not_5_out, OPCODE[2]);
  assign X_out = controlled_buffer_1_out;  // Buffer buffer_1, 4 bits wide
  assign Y_out = controlled_buffer_3_out;  // Buffer buffer_2, 4 bits wide
endmodule
