// Logisim project REGISTER.circ as structural Verilog: 4 circuits, main circuit main
module main (
  input  [3:0] Din,
  input  [2:0] R,
  input  Read,
  input  Write,
  input  [2:0] Rx,
  input  [2:0] Ry,
  input  [2:0] in_7,
  input  [3:0] in_8,
  input  in_9,
  input  in_10,
  input  in_11,
  output [3:0] out_12,
  output [3:0] out_13
);

  RegFile_8Reg regfile_8reg_1 (
    .RegNbr(R), .Sx(out_12), .Sy(out_13), .Write(Write), .Read(Read), .Din(Din), .Ry(Ry), .Rx(Rx));
  RAM #(.addrWidth(3), .dataWidth(4)) ram_1 (
    .addr(in_7), .data(in_8), .sel(in_9), .clk(in_10), .ld(in_11));  // open: clr
endmodule

// REGISTER
module REGISTER_4_bits (
  input  [3:0] D,
  input  CLK,
  input  READ,
  output [3:0] out_4
);

  wire dlatch_1_s, dlatch_2_s, dlatch_3_s, dlatch_4_s;

  DLatch dlatch_1 (.S(dlatch_1_s), .D(D[3]), .CLK(CLK));  // open: S_B
  and and_1 (out_4[3], READ, dlatch_1_s);
  DLatch dlatch_2 (.S(dlatch_2_s), .D(D[2]), .CLK(CLK));  // open: S_B
  and and_2 (out_4[2], READ, dlatch_2_s);
  DLatch dlatch_3 (.S(dlatch_3_s), .D(D[1]), .CLK(CLK));  // open: S_B
  and and_3 (out_4[1], READ, dlatch_3_s);
  DLatch dlatch_4 (.S(dlatch_4_s), .D(D[0]), .CLK(CLK));  // open: S_B
  and and_4 (out_4[0], READ, dlatch_4_s);
endmodule

// RegFile
module RegFile_8Reg (
  input  Write,
  input  Read,
  input  [3:0] Din,
  input  [2:0] RegNbr,
  input  [2:0] Ry,
  input  [2:0] Rx,
  output [3:0] Sx,
  output [3:0] Sy
);

  wire and_1_out, and_2_out, and_3_out, and_4_out, and_5_out, and_6_out, and_7_out, and_8_out,
       dec_3bit_1_out_2, dec_3bit_1_out_3, dec_3bit_1_out_4, dec_3bit_1_out_5, dec_3bit_1_out_6,
       dec_3bit_1_out_7, dec_3bit_1_out_8, dec_3bit_1_out_9;
  wire [3:0] register_4_bits_1_out_4, register_4_bits_2_out_4, register_4_bits_3_out_4,
       register_4_bits_4_out_4, register_4_bits_5_out_4, register_4_bits_6_out_4, register_4_bits_7_out_4,
       register_4_bits_8_out_4;

  DEC_3Bit dec_3bit_1 (
    .in_1(RegNbr), .out_2(dec_3bit_1_out_2), .out_3(dec_3bit_1_out_3), .out_4(dec_3bit_1_out_4),
    .out_5(dec_3bit_1_out_5), .out_6(dec_3bit_1_out_6), .out_7(dec_3bit_1_out_7), .out_8(dec_3bit_1_out_8),
    .out_9(dec_3bit_1_out_9));
  and and_1 (and_1_out, Write, dec_3bit_1_out_2);
  and and_2 (and_2_out, Write, dec_3bit_1_out_3);
  and and_3 (and_3_out, Write, dec_3bit_1_out_4);
  and and_4 (and_4_out, Write, dec_3bit_1_out_5);
  and and_5 (and_5_out, Write, dec_3bit_1_out_6);
  and and_6 (and_6_out, Write, dec_3bit_1_out_7);
  and and_7 (and_7_out, Write, dec_3bit_1_out_8);
  and and_8 (and_8_out, dec_3bit_1_out_9, Write);
  REGISTER_4_bits register_4_bits_1 (.CLK(and_1_out), .READ(Read), .D(Din), .out_4(register_4_bits_1_out_4));
  REGISTER_4_bits register_4_bits_2 (.CLK(and_2_out), .READ(Read), .D(Din), .out_4(register_4_bits_2_out_4));
  REGISTER_4_bits register_4_bits_3 (.CLK(and_3_out), .READ(Read), .D(Din), .out_4(register_4_bits_3_out_4));
  REGISTER_4_bits register_4_bits_4 (.CLK(and_4_out), .READ(Read), .D(Din), .out_4(register_4_bits_4_out_4));
  REGISTER_4_bits register_4_bits_5 (.CLK(and_5_out), .READ(Read), .D(Din), .out_4(register_4_bits_5_out_4));
  REGISTER_4_bits register_4_bits_6 (.CLK(and_6_out), .READ(Read), .D(Din), .out_4(register_4_bits_6_out_4));
  REGISTER_4_bits register_4_bits_7 (.CLK(and_7_out), .READ(Read), .D(Din), .out_4(register_4_bits_7_out_4));
  REGISTER_4_bits register_4_bits_8 (.CLK(and_8_out), .READ(Read), .D(Din), .out_4(register_4_bits_8_out_4));
  MUX_8__1_4_Bit mux_8_1_4_bit_1 (
    .in_9(Rx), .out_10(Sx), .in_1(register_4_bits_1_out_4), .in_2(register_4_bits_2_out_4),
    .in_3(register_4_bits_3_out_4), .in_4(register_4_bits_4_out_4), .in_5(register_4_bits_5_out_4),
    .in_6(register_4_bits_6_out_4), .in_7(register_4_bits_7_out_4), .in_8(register_4_bits_8_out_4));
  MUX_8__1_4_Bit mux_8_1_4_bit_2 (
    .in_9(Ry), .out_10(Sy), .in_1(register_4_bits_1_out_4), .in_2(register_4_bits_2_out_4),
    .in_3(register_4_bits_3_out_4), .in_4(register_4_bits_4_out_4), .in_5(register_4_bits_5_out_4),
    .in_6(register_4_bits_6_out_4), .in_7(register_4_bits_7_out_4), .in_8(register_4_bits_8_out_4));
endmodule

module RegFile (
  input  Write,
  input  Read,
  input  [3:0] Din,
  input  [1:0] RegSel,
  input  [1:0] Xsel,
  input  [1:0] Ysel,
  output [3:0] XOut,
  output [3:0] YOut
);

  wire and_1_out, and_2_out, and_3_out, and_4_out, dec_1_4_1_out_2, dec_1_4_1_out_3, dec_1_4_1_out_4,
       dec_1_4_1_out_5;
  wire [3:0] register_4_bits_1_out_4, register_4_bits_2_out_4, register_4_bits_3_out_4,
       register_4_bits_4_out_4;

  DEC_1_4 dec_1_4_1 (
    .in_1(RegSel), .out_2(dec_1_4_1_out_2), .out_3(dec_1_4_1_out_3), .out_4(dec_1_4_1_out_4),
    .out_5(dec_1_4_1_out_5));
  and and_1 (and_1_out, Write, dec_1_4_1_out_2);
  and and_2 (and_2_out, Write, dec_1_4_1_out_3);
  and and_3 (and_3_out, Write, dec_1_4_1_out_4);
  and and_4 (and_4_out, Write, dec_1_4_1_out_5);
  REGISTER_4_bits register_4_bits_1 (.CLK(and_1_out), .READ(Read), .D(Din), .out_4(register_4_bits_1_out_4));
  REGISTER_4_bits register_4_bits_2 (.CLK(and_2_out), .READ(Read), .D(Din), .out_4(register_4_bits_2_out_4));
  REGISTER_4_bits register_4_bits_3 (.CLK(and_3_out), .READ(Read), .D(Din), .out_4(register_4_bits_3_out_4));
  REGISTER_4_bits register_4_bits_4 (.CLK(and_4_out), .READ(Read), .D(Din), .out_4(register_4_bits_4_out_4));
  MUX_4__1_4Bit mux_4_1_4bit_1 (
    .Sel(Xsel), .out_6(XOut), .A(register_4_bits_1_out_4), .B(register_4_bits_2_out_4),
    .C(register_4_bits_3_out_4), .D(register_4_bits_4_out_4));
  MUX_4__1_4Bit mux_4_1_4bit_2 (
    .Sel(Ysel), .out_6(YOut), .A(register_4_bits_1_out_4), .B(register_4_bits_2_out_4),
    .C(register_4_bits_3_out_4), .D(register_4_bits_4_out_4));
endmodule
