// Logisim project lib.circ as structural Verilog: 11 circuits, main circuit main
module main (
  input  in_1,
  output out_2,
  output out_3
);

  wire clock_1_out;

  D_Flip_Flop d_ff_1 (.S_B(out_2), .S(out_3), .D(in_1), .CLK(clock_1_out));
  Clock clock_1 (.out(clock_1_out));
endmodule

module HALF_ADDER (
  input  A,
  input  B,
  output S,
  output out_4
);

  and and_1 (out_4, A, B);
  xor xor_1 (S, A, B);
endmodule

module MUX_2__1 (
  input  A,
  input  B,
  input  SEL,
  output S
);

  wire and_1_out, and_2_out, not_1_out;

  not not_1 (not_1_out, SEL);
  buf and_1 (and_1_out, B);  // AND_Gate
  and and_2 (and_2_out, A, not_1_out);
  or or_1 (S, and_1_out, and_2_out);
endmodule

module FULL_ADDER_1_Bit (
  input  A,
  input  B,
  input  C_i,
  output S,
  output C_o
);

  wire and_1_out, and_2_out, xor_1_out;

  xor xor_1 (xor_1_out, A, B);
  and and_1 (and_1_out, A, B);
  and and_2 (and_2_out, xor_1_out, C_i);
  xor xor_2 (S, xor_1_out, C_i);
  or or_1 (C_o, and_1_out, and_2_out);
endmodule

// DEC
module DEC_3Bit (
  input  a,
  input  b,
  input  c,
  output out_4,
  output out_5,
  output out_6,
  output out_7,
  output out_8,
  output out_9,
  output out_10,
  output out_11
);

  wire not_1_out, not_2_out, not_3_out;

  not not_1 (not_1_out, a);
  not not_2 (not_2_out, b);
  not not_3 (not_3_out, c);
  and and_1 (out_4, not_1_out, not_2_out, not_3_out);
  and and_2 (out_5, not_1_out, not_2_out, c);
  and and_3 (out_6, not_1_out, b, not_3_out);
  and and_4 (out_7, not_1_out, b, c);
  and and_5 (out_8, a, not_2_out, not_3_out);
  and and_6 (out_9, a, not_2_out, c);
  and and_7 (out_10, a, b, not_3_out);
  and and_8 (out_11, a, b, c);
endmodule

// MUX
module MUX_8__1_1Bit (
  input  in_1,
  input  in_2,
  input  in_3,
  input  in_4,
  input  in_5,
  input  in_6,
  input  in_7,
  input  in_8,
  input  [2:0] in_9,
  output out_10
);

  wire and_1_out, and_2_out, and_3_out, and_4_out, and_5_out, and_6_out, and_7_out, and_8_out, not_1_out,
       not_2_out, not_3_out;

  not not_1 (not_1_out, in_9[1]);
  not not_2 (not_2_out, in_9[2]);
  not not_3 (not_3_out, in_9[0]);
  and and_1 (and_1_out, in_1, not_2_out, not_1_out, not_3_out);
  and and_2 (and_2_out, in_2, not_2_out, not_1_out, in_9[0]);
  and and_3 (and_3_out, in_3, not_2_out, in_9[1], not_3_out);
  and and_4 (and_4_out, in_4, not_2_out, in_9[1], in_9[0]);
  and and_5 (and_5_out, in_5, in_9[2], not_1_out, not_3_out);
  and and_6 (and_6_out, in_6, in_9[2], not_1_out, in_9[0]);
  and and_7 (and_7_out, in_7, in_9[2], in_9[1], not_3_out);
  and and_8 (and_8_out, in_8, in_9[2], in_9[1], in_9[0]);
  or or_1 (out_10, and_1_out, and_2_out, and_3_out, and_4_out, and_5_out, and_6_out, and_7_out, and_8_out);
endmodule

module DLatch (
  input  D,
  input  CLK,
  output S_B,
  output S
);

  wire and_1_out, and_2_out, not_1_out;

  not not_1 (not_1_out, D);
  and and_1 (and_1_out, D, CLK);
  and and_2 (and_2_out, not_1_out, CLK);
  nor nor_1 (S_B, and_1_out, S);
  nor nor_2 (S, S_B, and_2_out);
endmodule

module MAJ (
  input  a,
  input  b,
  input  c,
  output out_4
);

  wire and_1_out, and_2_out, and_3_out, and_4_out, not_1_out, not_2_out, not_3_out;

  not not_1 (not_1_out, a);
  not not_2 (not_2_out, b);
  not not_3 (not_3_out, c);
  and and_1 (and_1_out, not_1_out, b, c);
  and and_2 (and_2_out, a, not_2_out, c);
  and and_3 (and_3_out, a, b, not_3_out);
  and and_4 (and_4_out, c, b, a);
  or or_1 (out_4, and_1_out, and_2_out, and_3_out, and_4_out);
endmodule

// COMP
module COMP_4Bit (
  input  [3:0] a,
  input  [3:0] b,
  output out_3
);

  wire xor_1_out, xor_2_out, xor_3_out, xor_4_out;

  xor xor_1 (xor_1_out, a[0], b[0]);
  xor xor_2 (xor_2_out, a[1], b[1]);
  xor xor_3 (xor_3_out, a[2], b[2]);
  xor xor_4 (xor_4_out, a[3], b[3]);
  nor nor_1 (out_3, xor_1_out, xor_2_out, xor_3_out, xor_4_out);
endmodule

// Decal_4B
module Decal_4Bit (
  input  [3:0] D,
  input  C,
  output [3:0] out_3
);

  wire and_1_out, and_3_out, and_4_out, and_6_out, not_1_out;

  not not_1 (not_1_out, C);
  and and_1 (and_1_out, D[0], C);
  and and_2 (out_3[0], not_1_out, D[1]);
  or or_1 (out_3[1], and_1_out, and_4_out);
  and and_3 (and_3_out, D[1], C);
  and and_4 (and_4_out, not_1_out, D[2]);
  or or_2 (out_3[2], and_3_out, and_6_out);
  and and_5 (out_3[3], D[2], C);
  and and_6 (and_6_out, not_1_out, D[3]);
endmodule

module D_Flip_Flop (
  input  D,
  input  CLK,
  output S_B,
  output S
);

  wire and_1_out, and_2_out, and_3_out, not_1_out, not_2_out;

  not not_1 (not_1_out, D);
  not not_2 (not_2_out, CLK);
  and and_1 (and_1_out, CLK, not_2_out);
  and and_2 (and_2_out, D, and_1_out);
  and and_3 (and_3_out, and_1_out, not_1_out);
  nor nor_1 (S_B, and_2_out, S);
  nor nor_2 (S, S_B, and_3_out);
endmodule
